// Digital circuit cmd.dig as structural Verilog
module cmd (
  input  [5:0] Co,
  input  [5:0] Nf,
  output beq,
  output bgtz,
  output blez,
  output bne,
  output cns,
  output d_m,
  output ereg,
  output jal,
  output jr,
  output ld,
  output M8,
  output mfhi,
  output mflo,
  output mx1,
  output Ns,
  output [3:0] Op,
  output shamt,
  output str
);

  wire addi, addiu, \and , andi, div, divu, lb, lui, lw, mult, multu, \nor , Op1, Op2, Op4, Op5, Op6, Op7,
       Op8, Op10, Op11, \or , ori, reg3, sb, slt, slti, sltiu, sltu, sub, subu, sw, \xor , xori;

  Decoder #(.Selector_Bits(6)) decoder_1 (
    .sel(Co), .out_0(reg3), .out_3(jal), .out_4(beq), .out_5(bne), .out_6(blez), .out_7(bgtz), .out_8(addi),
    .out_9(addiu), .out_10(slti), .out_11(sltiu), .out_12(andi), .out_13(ori), .out_14(xori), .out_15(lui),
    .out_32(lb), .out_35(lw), .out_36(cns), .out_40(sb), .out_43(sw));  // open: out_1, out_2, out_16, out_17, out_18, out_19, out_20, out_21, out_22, out_23, out_24, out_25, out_26, out_27, out_28, out_29, out_30, out_31, out_33, out_34, out_37, out_38, out_39, out_41, out_42, out_44, out_45, out_46, out_47, out_48, out_49, out_50, out_51, out_52, out_53, out_54, out_55, out_56, out_57, out_58, out_59, out_60, out_61, out_62, out_63
  // decodeur64 decodeur64_1: pin names not known; wires that end beside it: Nf, reg3, Op5, Op6, Op7, jr, mfhi, mflo, mult, multu, div, divu
  or or_1 (mx1, reg3, bne, beq);
  or or_2 (str, sw, sb);
  or or_3 (ld, lw, cns, lb);
  or or_4 (Ns, andi, ori, xori);
  or or_5 (shamt, Op5, Op6, Op7);
  nor nor_1 (ereg, sb, sw, jr, mult, multu, div, divu, bne, beq, bgtz, blez);
  or or_6 (M8, lb, cns, sb);
  or or_7 (d_m, mult, multu, div, divu);
  or or_8 (Op1, andi, \and );
  or or_9 (Op2, ori, \or );
  or or_10 (Op4, xori, \xor );
  or or_11 (Op8, sub, bne, beq, subu);
  or or_12 (Op10, slt, slti);
  or or_13 (Op11, sltu, sltiu);
  encodeur16 encodeur16_1 (
    ._0(1'b0), ._1(Op1), ._2(Op2), ._3(\nor ), ._4(Op4), ._5(Op5), ._6(Op6), ._7(Op7), ._8(Op8), ._9(lui),
    ._10(Op10), ._11(Op11), ._12(mult), ._13(multu), ._14(div), ._15(divu), .S(Op));

  // Other names for the same wires on the sheet: Op14 = div; Op15 = divu; lbu = cns; Op9 = lui; Op12 = mult;
  //   Op13 = multu; Op3 = \nor ; sll = Op5; sra = Op7; srl = Op6

  // Notes on the sheet:
  //   beq: pilote multoplexeur 1
  //   blez: pilote multoplexeur 1
  //   bne: pilote multoplexeur 1
  //   cns: jalr
  //   d_m: jalr
  //   ereg: pilote multoplexeur 1
  //   jal: jal
  //   jr: jr
  //   ld: lecture mémoire
  //   M8: lecture mémoire
  //   mfhi: pilote multoplexeur 1
  //   Co: Co de l'instruction
  //   Nf: Numéro de fonction
  //   mflo: pilote multoplexeur 1
  //   mx1: pilote multoplexeur 1, si=1 valeur rt comme deuxième opérande
  //   Ns: opérande non signée
  //   Op: Opération UAL, 5 bits
  //   shamt: Valeur shamt utilisée pour le décalage
  //   str: écriture mémoire
  //   Circuit de commande à compléter Novembre 2020
  //   A compléter
endmodule

/* Test case:
Co	Nf	Op	mx1	str	ld	bne	beq	Ns	shamt	ereg	M8	blez	bgtz	jal	jr	cns	mflo	mfhi	d/m	#	Instruction
0	0	5	1	0	0	0	0	0	1	1	0	0	0	0	0	0	0	0	0	#	sll
0	2	6	1	0	0	0	0	0	1	1	0	0	0	0	0	0	0	0	0	#	srl
0	3	7	1	0	0	0	0	0	1	1	0	0	0	0	0	0	0	0	0	#	sra
0	8	0	1	0	0	0	0	0	0	0	0	0	0	0	1	0	0	0	0	#	jr
0	16	0	1	0	0	0	0	0	0	1	0	0	0	0	0	0	0	1	0	#	mfhi
0	18	0	1	0	0	0	0	0	0	1	0	0	0	0	0	0	1	0	0	#	mflo
0	24	12	1	0	0	0	0	0	0	0	0	0	0	0	0	0	0	0	1	#	mult
0	25	13	1	0	0	0	0	0	0	0	0	0	0	0	0	0	0	0	1	#	multu
0	26	14	1	0	0	0	0	0	0	0	0	0	0	0	0	0	0	0	1	#	div
0	27	15	1	0	0	0	0	0	0	0	0	0	0	0	0	0	0	0	1	#	divu
0	32	0	1	0	0	0	0	0	0	1	0	0	0	0	0	0	0	0	0	#	add
0	33	0	1	0	0	0	0	0	0	1	0	0	0	0	0	0	0	0	0	#	addu
0	34	8	1	0	0	0	0	0	0	1	0	0	0	0	0	0	0	0	0	#	sub
0	35	8	1	0	0	0	0	0	0	1	0	0	0	0	0	0	0	0	0	#	subu
0	36	1	1	0	0	0	0	0	0	1	0	0	0	0	0	0	0	0	0	#	and
0	37	2	1	0	0	0	0	0	0	1	0	0	0	0	0	0	0	0	0	#	or
0	38	4	1	0	0	0	0	0	0	1	0	0	0	0	0	0	0	0	0	#	xor
0	39	3	1	0	0	0	0	0	0	1	0	0	0	0	0	0	0	0	0	#	nor
0	42	10	1	0	0	0	0	0	0	1	0	0	0	0	0	0	0	0	0	#	slt
0	43	11	1	0	0	0	0	0	0	1	0	0	0	0	0	0	0	0	0	#	sltu
3	0	0	0	0	0	0	0	0	0	1	0	0	0	1	0	0	0	0	0	#	jal
4	0	8	1	0	0	0	1	0	0	0	0	0	0	0	0	0	0	0	0	#	beq
5	0	8	1	0	0	1	0	0	0	0	0	0	0	0	0	0	0	0	0	#	bne
6	0	0	0	0	0	0	0	0	0	0	0	1	0	0	0	0	0	0	0	#	blez
7	0	0	0	0	0	0	0	0	0	0	0	0	1	0	0	0	0	0	0	#	bgtz
8	0	0	0	0	0	0	0	0	0	1	0	0	0	0	0	0	0	0	0	#	addi
9	0	0	0	0	0	0	0	0	0	1	0	0	0	0	0	0	0	0	0	#	addiu
10	0	10	0	0	0	0	0	0	0	1	0	0	0	0	0	0	0	0	0	#	slti
11	0	11	0	0	0	0	0	0	0	1	0	0	0	0	0	0	0	0	0	#	sltiu
12	0	1	0	0	0	0	0	1	0	1	0	0	0	0	0	0	0	0	0	#	andi
13	0	2	0	0	0	0	0	1	0	1	0	0	0	0	0	0	0	0	0	#	ori
14	0	4	0	0	0	0	0	1	0	1	0	0	0	0	0	0	0	0	0	#	xori
15	0	9	0	0	0	0	0	0	0	1	0	0	0	0	0	0	0	0	0	#	lui
32	0	0	0	0	1	0	0	0	0	1	1	0	0	0	0	0	0	0	0	#	lb
35	0	0	0	0	1	0	0	0	0	1	0	0	0	0	0	0	0	0	0	#	lw
36	0	0	0	0	1	0	0	0	0	1	1	0	0	0	0	1	0	0	0	#	lbu
40	0	0	0	1	0	0	0	0	0	0	1	0	0	0	0	0	0	0	0	#	sb
43	0	0	0	1	0	0	0	0	0	0	0	0	0	0	0	0	0	0	0	#	sw
*/
