// Digital circuit mips.dig as structural Verilog
module mips (
  input  C,
  output [31:0] cp,
  output [31:0] res
);

  wire and_1_out, and_2_out, and_3_out, and_4_out, and_5_out, and_6_out, and_7_out, beq, bgtz, blez, bne,
       cns, comparator_1_eq, comparator_2_eq, comparator_3_eq, comparator_4_eq, d_m, Data_p10, Data_p11,
       delay_1_out, eq_0, ereg, jal, jr, ld, lt_0, lt__eq_0, mem_8, mfhi, mflo, mx_1, mx_br, mx_shamt, Ns,
       or_1_out, str;
  wire [0:0] keyboard_1_av;
  wire [3:0] Op_ual;
  wire [4:0] multiplexer_2_out, multiplexer_6_out;
  wire [5:0] Co;
  wire [15:0] keyboard_1_d;
  wire [23:0] Data_p8, meminst_1_p4;
  wire [27:2] Imm26;
  wire [31:0] add_2_s, cp_plus_4, cp_q, Data_p7, Data_p9, data_read, HI, Imms, Imms_lt__lt_2, LO, mem_read,
       meminst_1_p2, multiplexer_1_out, multiplexer_3_out, multiplexer_4_out, multiplexer_5_out,
       multiplexer_7_out, multiplexer_8_out, multiplexer_9_out, multiplexer_10_out, multiplexer_12_out,
       multiplexer_13_out, multiplexer_14_out, multiplexer_16_out, ual_1_hi, ual_1_lo, val_rs, val_rt;

  Add #(.Bits(32)) add_1 (.a(cp), .b(32'h4), .c_i(1'b0), .s(cp_plus_4));  // open: c_o
  Add #(.Bits(32)) add_2 (.a(cp_plus_4), .b(Imms_lt__lt_2), .c_i(1'b0), .s(add_2_s));  // open: c_o
  Multiplexer #(.Bits(32)) multiplexer_1 (.sel(ld), .in_0(res), .in_1(data_read), .out(multiplexer_1_out));
  Multiplexer #(.Bits(5)) multiplexer_2 (.sel(mx_1), .in_0(Imm26[22:18]), .in_1(Imm26[17:13]), .out(multiplexer_2_out));
  Multiplexer #(.Bits(32)) multiplexer_3 (.sel(mx_br), .in_0(cp_plus_4), .in_1(add_2_s), .out(multiplexer_3_out));
  Multiplexer #(.Bits(32)) multiplexer_4 (.sel(mfhi), .in_0(multiplexer_1_out), .in_1(HI), .out(multiplexer_4_out));
  Comparator #(.Bits(32)) comparator_1 (.a(res), .b(32'hffff000c), .eq(comparator_1_eq));  // open: gt, lt
  Comparator #(.Bits(32)) comparator_2 (.a(res), .b(32'hffff0000), .eq(comparator_2_eq));  // open: gt, lt
  Comparator #(.Bits(32)) comparator_3 (.a(res), .b(32'hffff0004), .eq(comparator_3_eq));  // open: gt, lt
  Multiplexer #(.Bits(32)) multiplexer_5 (.sel(mflo), .in_0(multiplexer_4_out), .in_1(LO), .out(multiplexer_5_out));
  Multiplexer #(.Bits(5)) multiplexer_6 (
    .sel(jal), .in_0(multiplexer_2_out), .in_1({5{1'b1}}), .out(multiplexer_6_out));
  and and_1 (and_1_out, comparator_1_eq, str);
  and and_2 (and_2_out, comparator_2_eq, ld);
  and and_3 (and_3_out, comparator_3_eq, ld);
  Delay delay_1 (.in(C), .out(delay_1_out));
  Multiplexer #(.Bits(32)) multiplexer_7 (.sel(jr), .in_0(multiplexer_3_out), .in_1(val_rs), .out(multiplexer_7_out));
  Multiplexer #(.Bits(32)) multiplexer_8 (
    .sel(jal), .in_0(multiplexer_5_out), .in_1(cp_plus_4), .out(multiplexer_8_out));
  Multiplexer #(.Bits(32)) multiplexer_9 (
    .sel(jal), .in_0(multiplexer_7_out), .in_1({4'b0000, Imm26, 2'b00}), .out(multiplexer_9_out));
  RegisterFile #(.AddrBits(5), .Bits(32)) registerfile_1 (
    .Din(multiplexer_8_out), .we(ereg), .Rw(multiplexer_6_out), .C(delay_1_out), .Ra(Imm26[27:23]),
    .Rb(Imm26[22:18]), .Da(val_rs), .Db(val_rt));
  Keyboard keyboard_1 (.C(C), .en(and_3_out), .D(keyboard_1_d), .av(keyboard_1_av[0]));
  Register #(.Bits(32)) u_cp (.D(multiplexer_9_out), .C(~C), .en(1'b1), .Q(cp_q));
  Comparator #(.Bits(32)) comparator_4 (.a(cp_q), .b({32{1'b0}}), .eq(comparator_4_eq));  // open: gt, lt
  Multiplexer #(.Bits(32)) multiplexer_10 (
    .sel(and_3_out), .in_0(mem_read), .in_1({{16{1'b0}}, keyboard_1_d}), .out(multiplexer_10_out));
  Multiplexer #(.Bits(32)) multiplexer_11 (.sel(comparator_4_eq), .in_0(cp_q), .in_1(32'h400000), .out(cp));
  Multiplexer #(.Bits(32)) multiplexer_12 (
    .sel(mx_shamt), .in_0(val_rs), .in_1({{27{1'b0}}, Imm26[12:8]}), .out(multiplexer_12_out));
  Multiplexer #(.Bits(32)) multiplexer_13 (
    .sel(Ns), .in_0(Imms), .in_1({{16{1'b0}}, Imm26[17:2]}), .out(multiplexer_13_out));
  Multiplexer #(.Bits(32)) multiplexer_14 (
    .sel(mx_1), .in_0(multiplexer_13_out), .in_1(val_rt), .out(multiplexer_14_out));
  or or_1 (or_1_out, bgtz, blez);
  Multiplexer #(.Bits(32)) multiplexer_15 (
    .sel(and_2_out), .in_0(multiplexer_10_out), .in_1({{31{1'b0}}, keyboard_1_av[0]}), .out(data_read));
  Multiplexer #(.Bits(32)) multiplexer_16 (
    .sel(or_1_out), .in_0(multiplexer_14_out), .in_1({32{1'b0}}), .out(multiplexer_16_out));
  ual ual_1 (
    .A(multiplexer_12_out), .B(multiplexer_16_out), .Op(Op_ual), .S(res), .eq_0(eq_0), .lt__eq_0(lt__eq_0),
    .lt_0(lt_0), .HI(ual_1_hi), .LO(ual_1_lo));
  Terminal terminal_1 (.D(val_rt), .C(C), .en(and_1_out));
  // memInst meminst_1: pin names not known; wires that end beside it: cp, meminst_1_p2, {Co, Imm26}, meminst_1_p4
  ROM #(.AddrBits(24), .Bits(32)) rom_1 (.A(meminst_1_p4), .sel(1'b1), .D(meminst_1_p2));
  Register #(.Bits(32)) u_HI (.D(ual_1_hi), .C(C), .en(d_m), .Q(HI));
  Register #(.Bits(32)) u_LO (.D(ual_1_lo), .C(C), .en(d_m), .Q(LO));
  // memData Data: pin names not known; wires that end beside it: res, val_rt, str, ld, mem_8, cns, Data_p7, Data_p8, Data_p9, Data_p10, Data_p11, mem_read
  BarrelShifter #(.Bits(32)) barrelshifter_1 (.in(Imms), .shift(6'b000010), .out(Imms_lt__lt_2));
  BitExtender #(.inputBits(16), .outputBits(32)) bitextender_1 (.in(Imm26[17:2]), .out(Imms));
  EEPROMDualPort #(.AddrBits(24), .Bits(32)) \Donnée  (
    .A(Data_p8), .Din(Data_p9), .str(Data_p10), .C(C), .ld(Data_p11), .D(Data_p7));
  // cmd cmd_1: pin names not known; wires that end beside it: Co, Imm26[7:2], Imm26[22:18], beq, bgtz, blez, bne, cns, d_m, ereg, jal, jr, ld, mem_8, mfhi, mflo, mx_1, Ns, Op_ual, mx_shamt, str
  and and_4 (and_4_out, bne, ~eq_0);  // And
  and and_5 (and_5_out, beq, eq_0);
  and and_6 (and_6_out, bgtz, ~lt__eq_0);  // And
  and and_7 (and_7_out, blez, lt__eq_0);
  or or_2 (mx_br, and_4_out, and_5_out, and_6_out, and_7_out);

  // Other names for the same wires on the sheet: ImmNs[15:0] = Imm26[17:2]; Nf[5:0] = Imm26[7:2];
  //   shamt[4:0] = Imm26[12:8]; num_rd[4:0] = Imm26[17:13]; num_rt[4:0] = Imm26[22:18]; num_rs[4:0] = Imm26[27:23];
  //   res_ual[31:0] = res

  // Notes on the sheet:
  //   C: Hz: 1000
  //   mips complet à compléter Novembre 2020
  //   ?6
  //   contents of rom_1 (hex, n*v repeats v):
  //   ff7f013c,fcef3d34,f903100c,ffff1012,f0ffbd27,1000a4af,1400a5af,800a0af,b000010,1400a38f,
  //   800a28f,21106200,1000a48f,800a38f,21188300,6380,43a0,800a28f,1004224,800a2af,1000a38f,
  //   800a28f,21106200,4280,f0ff4014,1400a38f,800a28f,21106200,40a0,1000bd27,800e003,a4af,
  //   400a5af,3000010,400a28f,1004224,400a2af,400a28f,4280,faff4014,a000010,a28f,4380,400a28f,
  //   43a0,400a28f,1004224,400a2af,a28f,1004224,a2af,a28f,4280,f3ff4014,400a28f,40a0,800e003,
  //   d8ffbd27,2400bfaf,2800a4af,2c00a5af,1800a0af,1c00a0af,2800a28f,2000422c,e004014,1000224,
  //   17000010,110023c,4324,1c00a28f,21106200,4280,3004014,1800a28f,1004224,1800a2af,1c00a28f,
  //   1004224,1c00a2af,1800a38f,2800a28f,f1ff6214,1c00a38f,110023c,4224,21106200,2c00a58f,
  //   21200200,400100c,21100000,2400bf8f,2800bd27,800e003,e0ffbd27,1c00bfaf,2000a4af,2400a5af,
  //   2800a6af,2000a28f,80110200,c21e0200,2400a28f,43ac,2400a28f,428c,2800a58f,21200200,
  //   3900100c,1c00bf8f,2000bd27,800e003,e0ffbd27,1c00bfaf,2000a4af,2400a5af,2800a6af,2000a28f,
  //   c0120200,c21e0200,2400a28f,43ac,2400a28f,428c,2800a58f,21200200,3900100c,1c00bf8f,
  //   2000bd27,800e003,e0ffbd27,1c00bfaf,2000a4af,2400a5af,2800a6af,2000a28f,140200,c21e0200,
  //   2400a28f,43ac,2400a28f,428c,2800a58f,21200200,3900100c,1c00bf8f,2000bd27,800e003,
  //   a4af,a28f,a00422c,7004014,a28f,ff004230,37004224,ff004230,160200,3160200,6000010,
  //   a28f,ff004230,30004224,ff004230,160200,3160200,800e003,d8ffbd27,2400bfaf,2800a4af,
  //   2c00a5af,2c00a28f,30000324,43a0,2c00a28f,1004224,2c00a2af,2c00a28f,78000324,43a0,
  //   2c00a28f,1004224,2c00a2af,8000224,1800a2af,2800a28f,9004014,1000224,1800a2af,9000010,
  //   2800a28f,110200,2800a2af,1800a28f,ffff4224,1800a2af,2800a28f,2170200,f7ff4010,2800a28f,
  //   2170200,21200200,9400100c,21180200,2c00a28f,43a0,2800a28f,110200,2800a2af,2c00a28f,
  //   1004224,2c00a2af,1800a28f,ffff4224,1800a2af,1800a28f,eeff4014,2c00a28f,40a0,2400bf8f,
  //   2800bd27,800e003,d8ffbd27,2400bfaf,2800a4af,2c00a5af,2800a28f,9004104,2c00a28f,2d000324,
  //   43a0,2c00a28f,1004224,2c00a2af,2800a28f,23100200,2800a2af,2800a28f,1800a2af,1800a38f,
  //   a000224,1a006200,10100000,12100000,1800a2af,2c00a28f,1004224,2c00a2af,1800a28f,f5ff4014,
  //   2c00a28f,40a0,2c00a28f,ffff4224,2c00a2af,2800a38f,a000224,1a006200,10100000,21200200,
  //   9400100c,21180200,2c00a28f,43a0,2800a38f,a000224,1a006200,10100000,12100000,2800a2af,
  //   2800a28f,ecff4014,2400bf8f,2800bd27,800e003,d8ffbd27,2400bfaf,2800a4af,2c00a5af,3000a6af,
  //   2800a28f,1800a2af,1800a28f,140200,31c0200,2c00a28f,43ac,2c00a28f,428c,3000a58f,21200200,
  //   dd00100c,2400bf8f,2800bd27,800e003,e0ffbd27,1c00bfaf,2000a4af,2400a5af,2800a6af,2000a38f,
  //   2400a28f,43ac,2400a28f,428c,804230,6004014,2400a28f,428c,ffff4330,2400a28f,43ac,9000010,
  //   2400a28f,428c,21180200,ffff013c,2234,25106200,21180200,2400a28f,43ac,2400a28f,428c,
  //   2800a58f,21200200,a600100c,1c00bf8f,2000bd27,800e003,d8ffbd27,2400bfaf,2800a4af,2c00a5af,
  //   3000a6af,2800a28f,ffff4230,1800a2af,2c00a28f,1800a38f,43ac,3000a58f,1800a48f,a600100c,
  //   2400bf8f,2800bd27,800e003,d8ffbd27,2400bfaf,2800a4af,2c00a5af,3000a6af,2800a38f,ff03013c,
  //   2234,ffff4234,24106200,80100200,1800a2af,2c00a28f,1800a38f,43ac,3000a58f,1800a48f,
  //   a600100c,2400bf8f,2800bd27,800e003,e0ffbd27,1c00bfaf,2000a4af,2400a5af,2800a6af,2000a28f,
  //   40150200,c21e0200,2400a28f,43ac,2400a28f,428c,2800a58f,21200200,dd00100c,1c00bf8f,
  //   2000bd27,800e003,d8ffbd27,2400bfaf,2800a4af,2c00a5af,3000a6af,3400a7af,2800a28f,821e0200,
  //   2c00a28f,43ac,2800a28f,3f004330,3000a28f,43ac,1800a0af,1c00a0af,2c00a28f,428c,25004014,
  //   c000010,110023c,4e014324,1c00a28f,21106200,4280,3004014,1800a28f,1004224,1800a2af,
  //   1c00a28f,1004224,1c00a2af,3000a28f,438c,1800a28f,f0ff6214,1c00a38f,110023c,4e014224,
  //   21106200,3400a58f,21200200,400100c,1a000010,110023c,91004324,1c00a28f,21106200,4280,
  //   3004014,1800a28f,1004224,1800a2af,1c00a28f,1004224,1c00a2af,2c00a28f,438c,1800a28f,
  //   f0ff6214,3000a28f,ffff0324,43ac,1c00a38f,110023c,91004224,21106200,3400a58f,21200200,
  //   400100c,3400a28f,4380,58000224,6006214,3400a58f,110023c,24024424,400100c,1000224,
  //   1000010,21100000,2400bf8f,2800bd27,800e003,e0fbbd27,1c04bfaf,2004a4af,2404a5af,2404a28f,
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  //   contents of Donnée (hex, n*v repeats v):
  //   24300024,61740024,76300024,76310024,61300024,61310024,61320024,61330024,74300024,
  //   74310024,74320024,74330024,74340024,74350024,74360024,74370024,73300024,73310024,
  //   73320024,73330024,73340024,73350024,73360024,73370024,74380024,74390024,6b300024,
  //   6b310024,67700024,73700024,66700024,72610000,30313233,34353637,38394142,43444546,
  //   580058,58006a,616c2000,62657120,626e65,2000626c,657a2000,6267747a,20006164,64692000,
  //   61646469,75200073,6c746920,736c74,69752000,616e6469,20006f72,69200078,6f726920,6c7569,
  //   20005800,58005800,58005800,58005800,58005800,58005800,58005800,58005800,58006c62,
  //   20005800,58006c77,20006c62,75200058,580058,736220,580058,737720,580058,580058,580058,
  //   580058,580058,580058,580058,580058,580058,580058,736c,6c200058,73726c,20007372,61200073,
  //   6c6c7620,580073,726c7620,737261,7620006a,72200058,580058,737973,63616c6c,580058,58006d,
  //   66686920,58006d,666c6f20,580058,580058,58006d,756c7420,6d756c,74752000,64697620,646976,
  //   75200058,580058,580061,64642000,61646475,20007375,62200073,75627520,616e64,20006f72,
  //   2000786f,7220006e,6f722000,58005800,736c7420,736c74,75200058,580058,580058,580058,
  //   580058,580058,580058,580058,580058,580058,580000,23496e73,74727563,74696f6e,20696e63,
  //   6f6e6e75,65002c00,28002900,a000000,6000424,600100c,21200200,1000224,c000000,ffff0010,
  //   1000224,a4af,fcffbd23,18008200,12100000,ffff8420,faff8010,fcffbd23,a48f,800e003
endmodule

/* Test case:
C 	cp 		res
0 	0x400000	0x7FFF0000
C 	0x400004	0x7FFFEFFC
C 	0x400008	0x20020000
C 	0x40000C	0x2
C 	0x400010	X
C 	0x400014	X
C 	0x400018	0x10010000 	#lb $a0,0($t0)
C 	0x40001C	0x48 		#blez $a0,fin
C 	0x400020	x		#jal putChar
C 	0x400030	0x7FFFEFFC	#sw $t0,0($sp)
C 	0x400034	0x7FFFEFF8	#addi $sp,$sp-4
C 	0x400038	0xFFFF0000	#lui $t0,0x1001
C 	0x40003C	0xFFFF000C	#sw $a0,0xC($t0)
C 	0x400040	0x7FFFEFFC	#addi $sp,$sp-4
C 	0x400044	0x7FFFEFFC	#lw $t0,0(sp)
C 	0x400048	0x400024	#jr $ra
C 	0x400024	0x10010001	#addi $t0,$t0,1
C 	0x400028	0x48		#bgtz $t0,boucle
C 	0x400018	0x10010001	#lb $a0,0($t0)
C 	0x40001C	0x65 		#blez $a0,fin


#.data
#	chaine : .ascii "Hello world"
#.text
#	lui $t0,0x7FFF
#	ori $sp,$t0,0xEFFC
#	lui $t0,0x2002
#	li  $t1,2
#	div $t0,$t1
#	mflo $t0
#boucle:
#	lb $a0,0($t0)
#	blez $a0,fin
#	jal putChar
#	addi $t0,$t0,1
#	bgtz $a0,boucle
#fin:
#	beq $0,$0,fin
	

#putChar:
#	sw $t0,0($sp)
#	addi $sp,$sp,-4
#	lui $t0,0xFFFF
#	sw $a0,0xC($t0)
#	addi $sp,$sp,4
#	lw $t0,0($sp)
#	jr $ra
*/
